// Logisim project ex2.circ as structural Verilog: 1 circuit, main circuit AddMachine
module AddMachine (
  output [7:0] ADD_OUT,
  output [7:0] REG_OUT
);

  wire clock_1_out;
  wire [7:0] adder_1_out;

  Adder adder_1 (.a(8'h1), .out(adder_1_out));  // open: b, cin, cout
  Clock clock_1 (.out(clock_1_out));
  Register register_1 (.D(adder_1_out), .clk(clock_1_out));  // open: en, Q, clr

  // Notes on the sheet:
  //   PUT CIRCUITRY HERE
endmodule
