// Logisim project ex2_test.circ as structural Verilog: 1 circuit, main circuit main
module main (
  output [7:0] ADD_OUT,
  output [7:0] REG_OUT,
  output halt
);

  wire clock_1_out;
  wire [7:0] adder_1_out, register_1_q;

  Register register_1 (.D(adder_1_out), .clk(clock_1_out), .Q(register_1_q));  // open: en, clr
  Clock clock_1 (.out(clock_1_out));
  AddMachine addmachine_1 (.ADD_OUT(ADD_OUT), .REG_OUT(REG_OUT));
  Adder adder_1 (.a(8'h1), .b(register_1_q), .out(adder_1_out));  // open: cin, cout
  Comparator comparator_1 (.a(register_1_q), .b({8{1'b1}}), .eq(halt));  // open: gt, lt

  // Notes on the sheet:
  //   Your AddMachine circuit must fit here!
  //   There should be no red or blue wires, and the result should not be all X's
endmodule
